# Fritzing sketch schematic (saved by Fritzing 0.9.3b)
breadboards: 1

parts:
  S1 = Pushbutton [package="[THT]"]
  S2 = Pushbutton [package="[THT]"]
  S3 = Pushbutton [package="[THT]"]
  Part1 = Arduino Mega 2560 (Rev3)
  R1 = Resistor [tolerance=±5% resistance=220 package=THT]
  R2 = Resistor [tolerance=±5% resistance=220 package=THT]
  R3 = Resistor [tolerance=±5% resistance=220 package=THT]
  J2 = Piezo Speaker
  J1 = 0.91 inch OLED display 128x32 I2C SSD1306 [form="♂ (male)" package=THT]

nets:
  5V: S1.Pin_1, S1.Pin_2, S2.Pin_1, S2.Pin_2, S3.Pin_1, S3.Pin_2, Part1.5V, J1.VCC
  N1: S1.Pin_3, S1.Pin_4, Part1.D8_PWM, R1.Pin_0
  N2: S2.Pin_3, S2.Pin_4, Part1.D7_PWM, R2.Pin_0
  N3: S3.Pin_3, S3.Pin_4, Part1.D6_PWM, R3.Pin_0
  N4: Part1.D21/SCL, J1.SCL
  N5: Part1.D20/SDA, J1.SDA
  GND: Part1.GND, R1.Pin_1, R2.Pin_1, R3.Pin_1, J2.pin1, J1.GND
  N6: Part1.D11_PWM, J2.pin2
